// Logisim project processador.circ as structural Verilog
module dual_port_ram (
  input  [7:0] addr,
  input  [7:0] pc,
  input  [7:0] d,
  input  w,
  output [7:0] instr,
  output [7:0] data
);

  wire clock_1_out, or_1_out;
  wire [7:0] multiplexer_1_out;

  Clock clock_1 (.out(clock_1_out));
  or or_1 (or_1_out, w, clock_1_out);
  Multiplexer #(.width(8)) multiplexer_1 (.in0(addr), .in1(pc), .out(multiplexer_1_out), .sel(clock_1_out));
  RAM #(.asyncread("true")) ram_1 (
    .addr(multiplexer_1_out), .we(or_1_out), .oe(1'b1), .clk(clock_1_out), .din(d), .dout(data));
  Register #(.trigger("falling")) pcbuf (.D(data), .en(1'b1), .clk(clock_1_out), .Q(instr));  // open: clr
endmodule

module BancoDeRegistradores (
  input  [7:0] C,
  input  Clk,
  input  WriteReg,
  input  [1:0] RC,
  input  [1:0] RA,
  input  [1:0] RB,
  output [7:0] A,
  output [7:0] B
);

  wire demultiplexer_1_out0, demultiplexer_1_out1, demultiplexer_1_out2, demultiplexer_1_out3;
  wire [7:0] register_1_q, register_2_q, register_3_q, register_4_q;

  Demultiplexer #(.select(2)) demultiplexer_1 (
    .out0(demultiplexer_1_out0), .out1(demultiplexer_1_out1), .out2(demultiplexer_1_out2),
    .out3(demultiplexer_1_out3), .in(WriteReg), .sel(RC));
  Register register_1 (.D(C), .en(demultiplexer_1_out0), .clk(Clk), .Q(register_1_q));  // open: clr
  Register register_2 (.en(demultiplexer_1_out1), .clk(Clk), .Q(register_2_q));  // open: D, clr
  Register register_3 (.en(demultiplexer_1_out2), .clk(Clk), .Q(register_3_q));  // open: D, clr
  Register register_4 (.en(demultiplexer_1_out3), .clk(Clk), .Q(register_4_q));  // open: D, clr
  Multiplexer #(.select(2), .width(8)) multiplexer_1 (
    .in0(register_1_q), .in1(register_2_q), .in2(register_3_q), .in3(register_3_q), .out(A), .sel(RA));
  Multiplexer #(.select(2), .width(8)) multiplexer_2 (
    .in0(register_1_q), .in1(register_2_q), .in2(register_3_q), .in3(register_4_q), .out(B), .sel(RB));
endmodule

module ULA (
  input  [7:0] A,
  input  [7:0] B,
  input  [2:0] Funct,
  output Zero,
  output [7:0] S
);

  wire and_2_out, and_3_out, and_4_out, and_5_out, and_6_out, and_7_out;
  wire [7:0] adder_1_out, and_1_out, not_1_out, not_2_out, not_3_out, or_1_out, shifter_1_out, shifter_2_out,
       subtractor_1_out, xor_1_out;

  assign not_1_out = ~B;  // NOT_Gate not_1, 8 bits wide
  assign not_2_out = ~B;  // NOT_Gate not_2, 8 bits wide
  assign and_1_out = A & B;  // AND_Gate and_1, 8 bits wide
  assign or_1_out = A | B;  // OR_Gate or_1, 8 bits wide
  assign xor_1_out = A ^ B;  // XOR_Gate xor_1, 8 bits wide
  Adder adder_1 (.a(A), .b(B), .out(adder_1_out), .cin(1'b0));  // open: cout
  Subtractor subtractor_1 (.a(A), .b(not_1_out), .out(subtractor_1_out), .bin(1'b1));  // open: bout
  Shifter shifter_1 (.in(A), .out(shifter_1_out));  // open: dist
  Shifter #(.shift("lr")) shifter_2 (.in(B), .out(shifter_2_out));  // open: dist
  Multiplexer #(.select(3), .width(8)) multiplexer_1 (
    .in0(not_2_out), .in1(and_1_out), .in2(or_1_out), .in3(xor_1_out), .in4(adder_1_out),
    .in5(subtractor_1_out), .in6(shifter_1_out), .in7(shifter_2_out), .out(S), .sel(Funct));
  assign not_3_out = ~S;  // NOT_Gate not_3, 8 bits wide
  and and_2 (and_2_out, not_3_out[7], not_3_out[6]);
  and and_3 (and_3_out, not_3_out[5], not_3_out[4]);
  and and_4 (and_4_out, not_3_out[3], not_3_out[2]);
  and and_5 (and_5_out, not_3_out[1], not_3_out[0]);
  and and_6 (and_6_out, and_2_out, and_3_out);
  and and_7 (and_7_out, and_4_out, and_5_out);
  and and_8 (Zero, and_6_out, and_7_out);
endmodule
